// Logisim project labo_alu_etu.circ as structural Verilog: 12 circuits, main circuit ALU_MAXV
module ALU_MAXV (
  input  [3:0] a_i,
  input  [3:0] b_i,
  output [3:0] c_o
);

  wire alu_inst_erreur_o;
  wire [5:0] opcode_i_sw6;

  DipSwitch opcode_i (
    .sw1(opcode_i_sw6[5]), .sw2(opcode_i_sw6[4]), .sw3(opcode_i_sw6[3]), .sw4(opcode_i_sw6[2]),
    .sw5(opcode_i_sw6[1]), .sw6(opcode_i_sw6[0]));  // open: sw7, sw8
  ALU_Top alu_inst (.a_i(a_i), .b_i(b_i), .op_i(opcode_i_sw6), .c_o(c_o), .erreur_o(alu_inst_erreur_o));
  LED Error (.in(alu_inst_erreur_o));

  // Notes on the sheet:
  //   Attention, votre version de Logisim
  //   ne contient pas de tracker. Si vous
  //   enregistrez votre projet, toutes les
  //   informations du tracker seront
  //   définitivement effacées.
endmodule

module ALU_Top (
  input  [3:0] a_i,
  input  [3:0] b_i,
  input  [5:0] op_i,
  output [3:0] c_o,
  output erreur_o
);

  wire as_c, as_r3, as_z, oflow_o;
  wire [3:0] AddSub_r_o, Comparator_cmp_o, Custom_s_o, Logical_f_o;

  OpLogical Logical (.a_i(a_i), .b_i(b_i), .op_i(op_i[1:0]), .f_o(Logical_f_o));
  OpAddSub AddSub (
    .sel_in(op_i[3:2]), .A_in(a_i), .B_in(b_i), .O_out(oflow_o), .zero_o(as_z), .r3_o(as_r3),
    .r_o(AddSub_r_o), .carry_o(as_c));
  OpComp Comparator (
    .a3_i(a_i[3]), .b3_i(b_i[3]), .r3_i(as_r3), .zero_i(as_z), .carry_i(as_c), .op_i(op_i[2:0]),
    .cmp_o(Comparator_cmp_o));
  OpCustom Custom (.a_i(a_i), .s_o(Custom_s_o));
  error op_error (.op_i(op_i), .overflow_i(oflow_o), .error_o(erreur_o));
  Multiplexer #(.select(2), .width(4), .enable("false")) multiplexer_1 (
    .in0(AddSub_r_o), .in1(Comparator_cmp_o), .in2(Logical_f_o), .in3(Custom_s_o), .out(c_o), .sel(op_i[5:4]));

  // Other names for the same wires on the sheet: op_01[1:0] = op_i[1:0]; op_23[1:0] = op_i[3:2]; a3_i = a_i[3];
  //   b3_i = b_i[3]; op_45[1:0] = op_i[5:4]

  // Notes on the sheet:
  //   Attention, votre version de Logisim
  //   ne contient pas de tracker. Si vous
  //   enregistrez votre projet, toutes les
  //   informations du tracker seront
  //   définitivement effacées.
endmodule

module Add1bit (
  input  a_i,
  input  b_i,
  input  c_i,
  output r_o,
  output c_o
);

  wire and_1_out, and_2_out, and_3_out, xor_1_out;

  xor xor_1 (xor_1_out, a_i, b_i);
  and and_1 (and_1_out, a_i, b_i);
  and and_2 (and_2_out, a_i, c_i);
  and and_3 (and_3_out, b_i, c_i);
  xor xor_2 (r_o, xor_1_out, c_i);
  or or_1 (c_o, and_1_out, and_2_out, and_3_out);

  // Notes on the sheet:
  //   Attention, votre version de Logisim
  //   ne contient pas de tracker. Si vous
  //   enregistrez votre projet, toutes les
  //   informations du tracker seront
  //   définitivement effacées.
endmodule

module Add4bit (
  input  c_i,
  input  [3:0] a_i,
  input  [3:0] b_i,
  output [3:0] r_o,
  output c_o
);

  wire Add1b_1_c_o, Add1b_2_c_o, Add1b_3_c_o;

  Add1bit Add1b_1 (.a_i(a_i[0]), .b_i(b_i[0]), .c_i(c_i), .r_o(r_o[0]), .c_o(Add1b_1_c_o));
  Add1bit Add1b_2 (.a_i(a_i[1]), .b_i(b_i[1]), .c_i(Add1b_1_c_o), .r_o(r_o[1]), .c_o(Add1b_2_c_o));
  Add1bit Add1b_3 (.a_i(a_i[2]), .b_i(b_i[2]), .c_i(Add1b_2_c_o), .r_o(r_o[2]), .c_o(Add1b_3_c_o));
  Add1bit Add1b_4 (.a_i(a_i[3]), .b_i(b_i[3]), .c_i(Add1b_3_c_o), .r_o(r_o[3]), .c_o(c_o));

  // Notes on the sheet:
  //   Attention, votre version de Logisim
  //   ne contient pas de tracker. Si vous
  //   enregistrez votre projet, toutes les
  //   informations du tracker seront
  //   définitivement effacées.
endmodule

module Sub4bit (
  input  [3:0] a_i,
  input  [3:0] b_i,
  output [3:0] r_o,
  output c_o
);

  wire [3:0] xor_1_out;

  assign xor_1_out = b_i ^ 4'b1111;  // XOR_Gate xor_1, 4 bits wide
  Add4bit Add4b_1 (.c_i(1'b1), .a_i(a_i), .b_i(xor_1_out), .r_o(r_o), .c_o(c_o));

  // Notes on the sheet:
  //   Attention, votre version de Logisim
  //   ne contient pas de tracker. Si vous
  //   enregistrez votre projet, toutes les
  //   informations du tracker seront
  //   définitivement effacées.
endmodule

module AddSub4bit (
  input  sel_i,
  input  [3:0] a_i,
  input  [3:0] b_i,
  output [3:0] r_o,
  output c_o
);

  wire [3:0] xor_1_out;

  assign xor_1_out = {4{sel_i}} ^ b_i;  // XOR_Gate xor_1, 4 bits wide
  Add4bit add4b_1 (.c_i(sel_i), .a_i(a_i), .b_i(xor_1_out), .r_o(r_o), .c_o(c_o));

  // Notes on the sheet:
  //   Attention, votre version de Logisim
  //   ne contient pas de tracker. Si vous
  //   enregistrez votre projet, toutes les
  //   informations du tracker seront
  //   définitivement effacées.
endmodule

module OpAddSub (
  input  [1:0] sel_in,
  input  [3:0] A_in,
  input  [3:0] B_in,
  output O_out,
  output zero_o,
  output r3_o,
  output [3:0] r_o,
  output carry_o
);

  AddSub4bit Addsub1 (.sel_i(sel_in[1]), .a_i(A_in), .b_i(B_in), .r_o({r3_o, r_o[2:0]}), .c_o(carry_o));
  Overflow Over_flow (.A3(A_in[3]), .B3(B_in[3]), .R3(r3_o), .C_in(carry_o), .Sel_in(sel_in), .O_out(O_out));
  nor nor_1 (zero_o, r_o[0], r_o[1], r_o[2], r3_o);

  assign r_o[3] = r3_o;

  // Notes on the sheet:
  //   Attention, votre version de Logisim
  //   ne contient pas de tracker. Si vous
  //   enregistrez votre projet, toutes les
  //   informations du tracker seront
  //   définitivement effacées.
endmodule

module OpComp (
  input  a3_i,
  input  b3_i,
  input  r3_i,
  input  zero_i,
  input  carry_i,
  input  [2:0] op_i,
  output [3:0] cmp_o
);

  wire and_1_out, and_2_out, and_3_out, and_4_out, not_1_out, not_2_out, or_1_out, or_2_out, xnor_1_out,
       xnor_2_out;

  not not_1 (not_1_out, zero_i);
  not not_2 (not_2_out, carry_i);
  xnor xnor_1 (xnor_1_out, a3_i, b3_i);
  xnor xnor_2 (xnor_2_out, a3_i, b3_i);
  and and_1 (and_1_out, ~a3_i, b3_i);  // AND_Gate
  and and_2 (and_2_out, xnor_1_out, ~r3_i);  // AND_Gate
  and and_3 (and_3_out, a3_i, ~b3_i);  // AND_Gate
  and and_4 (and_4_out, r3_i, xnor_2_out);
  or or_1 (or_1_out, and_1_out, and_2_out);
  or or_2 (or_2_out, and_3_out, and_4_out);
  Multiplexer #(.select(3), .enable("false")) multiplexer_1 (
    .in0(1'b0), .in1(or_1_out), .in2(or_2_out), .in3(not_1_out), .in4(zero_i), .in5(carry_i),
    .in6(not_2_out), .in7(1'b0), .out(cmp_o[0]), .sel(op_i));

  assign cmp_o[3:1] = 3'b000;

  // Notes on the sheet:
  //   Attention, votre version de Logisim
  //   ne contient pas de tracker. Si vous
  //   enregistrez votre projet, toutes les
  //   informations du tracker seront
  //   définitivement effacées.
  //   A = B
  //   A != B
  //   A >= B
  //   A < B
  //   A >= B
  //   A < B
endmodule

module OpLogical (
  input  [3:0] a_i,
  input  [3:0] b_i,
  input  [1:0] op_i,
  output [3:0] f_o
);

  wire [3:0] and_1_out, nand_1_out, or_1_out, xor_1_out;

  assign and_1_out = a_i & b_i;  // AND_Gate and_1, 4 bits wide
  assign or_1_out = a_i | b_i;  // OR_Gate or_1, 4 bits wide
  assign nand_1_out = ~(a_i & b_i);  // NAND_Gate nand_1, 4 bits wide
  assign xor_1_out = a_i ^ b_i;  // XOR_Gate xor_1, 4 bits wide
  Multiplexer #(.select(2), .width(4), .enable("false")) multiplexer_1 (
    .in0(and_1_out), .in1(or_1_out), .in2(nand_1_out), .in3(xor_1_out), .out(f_o), .sel(op_i));

  // Notes on the sheet:
  //   Attention, votre version de Logisim
  //   ne contient pas de tracker. Si vous
  //   enregistrez votre projet, toutes les
  //   informations du tracker seront
  //   définitivement effacées.
endmodule

module OpCustom (
  input  [3:0] a_i,
  output [3:0] s_o
);

  wire Add_1bit_c_o, Add_lsb_c_o, Add_lsb_r_o, Add_msb_c_o, Add_msb_r_o;

  Add1bit Add_lsb (.a_i(a_i[0]), .b_i(a_i[1]), .c_i(1'b0), .r_o(Add_lsb_r_o), .c_o(Add_lsb_c_o));
  Add1bit Add_msb (.a_i(a_i[2]), .b_i(a_i[3]), .c_i(1'b0), .r_o(Add_msb_r_o), .c_o(Add_msb_c_o));
  Add1bit Add_1bit (.a_i(Add_msb_r_o), .b_i(Add_lsb_r_o), .c_i(1'b0), .r_o(s_o[0]), .c_o(Add_1bit_c_o));
  Add1bit Add_2bits (.a_i(Add_lsb_c_o), .b_i(Add_msb_c_o), .c_i(Add_1bit_c_o), .r_o(s_o[1]), .c_o(s_o[2]));

  assign s_o[3] = 1'b0;

  // Notes on the sheet:
  //   Attention, votre version de Logisim
  //   ne contient pas de tracker. Si vous
  //   enregistrez votre projet, toutes les
  //   informations du tracker seront
  //   définitivement effacées.
endmodule

module Overflow (
  input  A3,
  input  B3,
  input  R3,
  input  C_in,
  input  [1:0] Sel_in,
  output O_out
);

  wire AddAB1_out, AddAB2_out, multiplexer_1_out, multiplexer_2_out, not_1_out, or_1_out, or_2_out,
       SubAB1_out, SubAB2_out;

  not not_1 (not_1_out, C_in);
  and AddAB1 (AddAB1_out, A3, B3, ~R3);  // AND_Gate
  and AddAB2 (AddAB2_out, ~A3, ~B3, R3);  // AND_Gate
  and SubAB1 (SubAB1_out, A3, ~B3, ~R3);  // AND_Gate
  and SubAB2 (SubAB2_out, ~A3, B3, R3);  // AND_Gate
  Multiplexer #(.enable("false")) multiplexer_1 (.in0(C_in), .in1(not_1_out), .out(multiplexer_1_out), .sel(Sel_in[1]));
  or or_1 (or_1_out, AddAB1_out, AddAB2_out);
  or or_2 (or_2_out, SubAB1_out, SubAB2_out);
  Multiplexer #(.enable("false")) multiplexer_2 (
    .in0(or_1_out), .in1(or_2_out), .out(multiplexer_2_out), .sel(Sel_in[1]));
  Multiplexer #(.enable("false")) multiplexer_3 (
    .in0(multiplexer_2_out), .in1(multiplexer_1_out), .out(O_out), .sel(Sel_in[0]));

  // Notes on the sheet:
  //   Attention, votre version de Logisim
  //   ne contient pas de tracker. Si vous
  //   enregistrez votre projet, toutes les
  //   informations du tracker seront
  //   définitivement effacées.
  //   Add/sub Selection
  //   Add/sub Selection
  //   Signed/Unsigned selection
endmodule

module error (
  input  [5:0] op_i,
  input  overflow_i,
  output error_o
);

  wire and_1_out, and_2_out, and_3_out, and_4_out;

  and and_1 (and_1_out, ~op_i[5], op_i[4], ~op_i[3]);  // AND_Gate
  and and_2 (and_2_out, ~op_i[5], op_i[4], op_i[3], op_i[2], op_i[1], op_i[0]);  // AND_Gate
  and and_3 (and_3_out, ~op_i[5], op_i[4], op_i[3], ~op_i[2], ~op_i[1], ~op_i[0]);  // AND_Gate
  and and_4 (and_4_out, ~op_i[5], ~op_i[4], overflow_i);  // AND_Gate
  or or_1 (error_o, and_1_out, and_2_out, and_3_out, and_4_out);

  // Other names for the same wires on the sheet: op_0 = op_i[0]; op_1 = op_i[1]; op_2 = op_i[2]; op_3 = op_i[3];
  //   op_4 = op_i[4]; op_5 = op_i[5]

  // Notes on the sheet:
  //   Attention, votre version de Logisim
  //   ne contient pas de tracker. Si vous
  //   enregistrez votre projet, toutes les
  //   informations du tracker seront
  //   définitivement effacées.
endmodule
